# Fritzing sketch ar20 led (saved by Fritzing 0.9.3b)
breadboards: 1

parts:
  부품1 = Arduino Uno (Rev3)
  R2 = Resistor [tolerance=±5% resistance=220 package=THT]
  R1 = Resistor [tolerance=±5% resistance=220 package=THT]
  LED2 = LED - 5mm [color="Red (633nm)" package="5 mm [THT]"]
  LED1 = smd LED [color="Green (560nm)" package="0603 [SMD]"]

nets:
  N1: 부품1.D4, LED2.anode
  N2: 부품1.D6_PWM, LED1.anode
  N3: 부품1.GND, R2.Pin_1
  N4: R2.Pin_0, LED2.cathode
  N5: R1.Pin_0, LED1.cathode
